# Fritzing sketch photointerrupter (saved by Fritzing 0.9.3b)
breadboards: 1

parts:
  Part1 = Arduino Uno (Rev3)
  Q1 = PHOTOTRANSISTOR REFLECTIVE OBJECT SENSOR [package=qrb1114-side]
  LED1 = smd LED [color="Red (633nm)" package="0805 [SMD]"]
  R1 = Resistor [tolerance=±5% resistance=220 package="0402 [SMD]"]

nets:
  N1: Part1.D13/SCK, LED1.cathode
  N2: Part1.D2, Part1.D3_PWM, Q1.E
  N3: Part1.GND, Q1.C, R1.Pin_1
  N4: Q1.A, Q1.K
  N5: LED1.anode, R1.Pin_0
